// Logisim project RS_Flipflop.circ as structural Verilog: 1 circuit, main circuit main
module main (
  input  in_1,
  input  in_2,
  input  in_3,
  input  in_4,
  input  in_5,
  input  in_6,
  input  in_7,
  input  in_8,
  input  in_9,
  input  in_10,
  input  in_11,
  output out_12,
  output out_13,
  output out_14,
  output out_15,
  output out_16,
  output out_17,
  output out_18,
  output out_19,
  output out_20,
  output out_21,
  output out_22,
  output out_23,
  output out_24
);

  wire and_1_out, clock_1_out, clock_2_out, nand_4_out, nand_5_out, nand_6_out, nand_7_out, nand_8_out,
       nand_9_out, nand_10_out, nand_11_out, nand_12_out, nand_19_out, nand_20_out, not_3_out, not_4_out,
       or_1_out, or_2_out, or_3_out;

  Clock clock_1 (.out(clock_1_out));
  Clock clock_2 (.out(clock_2_out));
  nand nand_1 (out_12, in_1, out_13);
  nand nand_2 (out_13, out_12, in_2);
  nand nand_3 (out_16, out_16, in_5);
  or or_1 (or_1_out, in_3, out_15);
  or or_2 (or_2_out, out_14, in_4);
  and and_1 (and_1_out, nand_5_out, clock_1_out);
  not not_1 (out_14, or_1_out);
  not not_2 (out_15, or_2_out);
  nand nand_4 (nand_4_out, nand_7_out, nand_5_out);
  nand nand_5 (nand_5_out, nand_4_out, clock_1_out);
  nand nand_6 (nand_6_out, and_1_out, nand_7_out);
  nand nand_7 (nand_7_out, nand_6_out, in_6);
  not not_3 (not_3_out, in_8);
  nand nand_8 (nand_8_out, nand_11_out, nand_9_out);
  nand nand_9 (nand_9_out, nand_8_out, clock_2_out);
  nand nand_10 (nand_10_out, nand_9_out, nand_11_out);
  nand nand_11 (nand_11_out, nand_10_out, in_11);
  nand nand_12 (nand_12_out, in_8, in_10);
  or or_3 (or_3_out, not_3_out, in_10);
  nand nand_13 (out_17, nand_5_out, out_18);
  nand nand_14 (out_18, out_17, nand_6_out);
  nand nand_15 (out_20, nand_12_out, out_22);
  nand nand_16 (out_22, out_20, or_3_out);
  nand nand_17 (out_23, nand_9_out, out_24);
  nand nand_18 (out_24, out_23, nand_10_out);
  nand nand_19 (nand_19_out, in_7, in_9);
  not not_4 (not_4_out, in_9);
  nand nand_20 (nand_20_out, in_7, not_4_out);
  nand nand_21 (out_19, nand_19_out, out_21);
  nand nand_22 (out_21, out_19, nand_20_out);
endmodule
